# Fritzing sketch UltrasonicWithsoundNledFeedback (saved by Fritzing 0.7.12b)
breadboards: 1

parts:
  Arduino1 = Arduino
  LED1 = LED - 5mm [color="Red (633nm)" package="5 mm [THT]"]
  J1 = Piezo Speaker
  Part1 = SRF05 Ultrasonic Rangefinder
  R1 = Resistor [tolerance=±5% resistance=220 package=THT]
  LED2 = LED - 5mm [color="Red (633nm)" package="5 mm [THT]"]
  R2 = Resistor [tolerance=±5% resistance=220 package=THT]
  LED3 = LED - 5mm [color="Yellow (595nm)" package="5 mm [THT]"]
  R3 = Resistor [tolerance=±5% resistance=220 package=THT]
  LED4 = LED - 5mm [color="Yellow (595nm)" package="5 mm [THT]"]
  R4 = Resistor [tolerance=±5% resistance=220 package=THT]
  LED5 = LED - 5mm [color="Green (570nm)" package="5 mm [THT]"]
  R5 = Resistor [tolerance=±5% resistance=220 package=THT]
  LED6 = LED - 5mm [color="Green (570nm)" package="5 mm [THT]"]
  R6 = Resistor [tolerance=±5% resistance=220 package=THT]
  R7 = Resistor [tolerance=±5% resistance=220 package=THT]

nets:
  N1: Arduino1.D12, Part1.Trig
  N2: Arduino1.D11, Part1.Echo
  N3: Arduino1.D8, R7.Pin_1
  N4: Arduino1.D7, R1.Pin_0
  N5: Arduino1.D6, R2.Pin_0
  N6: Arduino1.D5, R3.Pin_0
  N7: Arduino1.D4, R4.Pin_0
  N8: Arduino1.D3, R5.Pin_0
  N9: Arduino1.D2, R6.Pin_0
  +5V: Arduino1.+5V, Part1.VCC
  GND: Arduino1.GND, LED1.cathode, J1.pin1, Part1.GND, LED2.cathode, LED3.cathode, LED4.cathode, LED5.cathode, LED6.cathode
  N10: LED1.anode, R1.Pin_1
  N11: J1.pin2, R7.Pin_0
  N12: LED2.anode, R2.Pin_1
  N13: LED3.anode, R3.Pin_1
  N14: LED4.anode, R4.Pin_1
  N15: LED5.anode, R5.Pin_1
  N16: LED6.anode, R6.Pin_1
